# Fritzing sketch RPi ServoHut using PCA9685 (saved by Fritzing 0.9.3b)
perfboards: 1
breadboards: 1

parts:
  Raspberry_Pi_1 = Raspberry Pi 3 [part_number=RPI-3-V1.2]  # not connected
  R1 = Resistor [tolerance=±5% resistance=220 package=THT]
  LED1 = LED - 3mm [color="Yellow (595nm)" package="3 mm [THT]"]
  LED2 = LED - 3mm [color="Yellow (595nm)" package="3 mm [THT]"]
  LED3 = LED - 3mm [color="Yellow (595nm)" package="3 mm [THT]"]
  LED4 = LED - 3mm [color="Yellow (595nm)" package="3 mm [THT]"]
  LED5 = LED - 3mm [color="Yellow (595nm)" package="3 mm [THT]"]
  LED6 = LED - 3mm [color="Yellow (595nm)" package="3 mm [THT]"]
  LED7 = LED - 3mm [color="Yellow (595nm)" package="3 mm [THT]"]
  LED8 = LED - 3mm [color="Yellow (595nm)" package="3 mm [THT]"]
  J1 = female alternating pin header, 4 pins [form="♀ (female)"]
  J2 = female alternating pin header, 4 pins [form="♀ (female)"]
  VCC1 = 4 x AAA Battery Mount
  IC1 = ULN2803A [package=THT]
  IC2 = SO-28x [chip_label=PCA9685 package=SO(x)]  # not connected

nets:
  N1: R1.Pin_0, VCC1.+
  N2: R1.Pin_1, LED1.anode, LED2.anode, LED3.anode, LED4.anode, LED5.anode, LED6.anode, LED7.anode, LED8.anode
  N3: LED1.cathode, IC1.Out_4
  N4: LED2.cathode, IC1.Out_6
  N5: LED3.cathode, IC1.Out_5
  N6: LED4.cathode, IC1.Out_2
  N7: LED5.cathode, IC1.Out_7
  N8: LED6.cathode, IC1.Out_8
  N9: LED7.cathode, IC1.Out_3
  N10: LED8.cathode, IC1.Out_1
  N11: J1.pin1, IC1.In_4
  N12: J1.pin2, IC1.In_3
  N13: J1.pin3, IC1.In_2
  N14: J1.pin4, IC1.In_1
  N15: J2.pin1, IC1.In_8
  N16: J2.pin2, IC1.In_7
  N17: J2.pin3, IC1.In_6
  N18: J2.pin4, IC1.In_5
  N19: VCC1.-, IC1.0V

notes:
  Adafruit 16 channel PWM
